# Fritzing sketch esp_shield (saved by Fritzing 0.9.9b)
circuit board: 7.5cm x 5cm
breadboards: 1

parts:
  part = ESP32S-HiLetgo [part_number=ESP32S-HiLetgo]
  part_2 = M10X2 [package=2x10_lock]
  part_3 = M10X2 [package=2x10_lock]
  part_4 = M10X2 [package=2x10_lock]
  part_5 = M10X2 [package=2x10_lock]
  part_6 = M10X2 [package=2x10_lock]
  part_7 = M10X2 [package=2x10_lock]
  part_8 = M10X2 [package=2x10_lock]
  part_9 = M10X2 [package=2x10_lock]
  part_10 = M10X2 [package=2x10_lock]
  part_11 = M10X2 [package=2x10_lock]

nets:
  N1: part.3.3, part_11.13, part_11.15, part_11.17, part_11.19
  N2: part.EN, part_4.2
  N3: part.GPIO36, part_4.4
  N4: part.GPIO39, part_4.6
  N5: part.GPIO34, part_4.8
  N6: part.GPIO35, part_4.10
  N7: part.GPIO32, part_4.12
  N8: part.GPIO33, part_4.14
  N9: part.GPIO25, part_4.16
  N10: part.GPIO26, part_4.18
  N11: part.GPIO27, part_4.20
  N12: part.GPIO14, part_2.14
  N13: part.GPIO12, part_2.16
  N14: part.GND, part_2.18, part_3.13, part_3.15, part_3.17, part_3.19, part_5.1, part_5.3, part_5.5, part_5.7, part_5.9, part_5.11, part_5.13, part_5.15, part_5.17, part_5.19, part_6.1, part_7.1, part_8.2, part_8.4, part_8.6, part_8.8, part_8.10, part_8.12, part_9.2, part_9.4, part_9.6, part_9.8, part_9.10, part_9.12, part_9.14, part_9.16, part_9.18, part_9.20, part_11.2, part_11.4, part_11.6, part_11.8, part_11.10, part_11.12, part_11.14, part_11.16, part_11.18, part_11.20
  N15: part.GPIO13, part_2.20
  N16: part.VIN, part_3.20, part_7.16, part_9.7, part_9.9, part_9.11, part_9.13, part_9.15, part_9.17, part_9.19
  N17: part.GPIO15, part_7.19
  N18: part.GPIO2, part_7.17
  N19: part.GPIO0, part_7.15
  N20: part.GPIO4, part_7.13
  N21: part.GPIO16, part_7.11, part_10.13, part_10.15, part_10.17, part_10.19
  N22: part.GPIO17, part_7.9, part_10.14, part_10.16, part_10.18, part_10.20
  N23: part.GPIO5, part_7.7
  N24: part.GPIO18, part_7.5
  N25: part.GPIO19, part_7.3
  N26: part.GPIO21, part_6.11, part_10.2, part_10.4, part_10.6, part_10.8
  N27: part.GPIO3, part_6.9
  N28: part.GPIO1, part_6.7
  N29: part.GPIO22, part_6.5, part_10.1, part_10.3, part_10.5, part_10.7
  N30: part.GPIO23, part_6.3
  N31: part_2.1, part_5.2, part_5.4, part_5.6, part_5.8
  N32: part_2.3, part_5.10
  N33: part_2.5, part_5.12
  N34: part_2.7, part_5.14
  N35: part_2.9, part_5.16
  N36: part_2.11, part_5.18
  N37: part_2.19, part_3.14, part_3.16, part_3.18, part_5.20
  N38: part_6.2, part_11.1, part_11.3, part_11.5, part_11.7, part_11.9
  N39: part_6.14, part_8.1, part_8.3, part_8.5, part_8.7, part_8.9, part_8.11
  N40: part_6.16, part_9.1
  N41: part_6.18, part_9.3
  N42: part_6.20, part_9.5

notes:
  23
  22
  1
  21
  gnd
  3
  5
  16
  18
  17
  4
  2
  0
  15
  19
  13
  14
  32
  34
  35
  39
  36
  27
  25
  12
  33
  26
  Pins
  XXX
  X
  Design by Gpap
  5V
  GND
  SDA
  SLC
  RX2
  TX2
  3V3

custom parts:
  ESP32S-HiLetgo: HiLetgo ESP-WROOM-32 ESP32 ESP-32S Development Board 2.4GHz Dual-Mode WiFi + Bluetooth Dual Cores Microcontroller The ESP32 integrated with Antenna switches, RF Balun, power amplifiers, low-noise amplifiers, filters, and management modules, and the entire solution occupies the least area of PCB. 2.4 GHz Wi-Fi plus Bluetooth dual-mode chip, with TSMC Ultra-low power consumption 40nm technology,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
